// Logisim project 24125102_01.circ as structural Verilog: 1 circuit, main circuit main
module main (
  input  in_1,
  input  in_2,
  input  in_3,
  input  in_4,
  input  in_5,
  input  in_6,
  input  in_7,
  input  in_8
);

  wire and_1_out, and_2_out, and_3_out, and_4_out, and_5_out, and_6_out, and_7_out, and_8_out, and_9_out,
       and_10_out, and_11_out, and_12_out, and_13_out, and_14_out, and_15_out, and_16_out, not_1_out,
       not_2_out, not_3_out, not_4_out, or_1_out, or_2_out, or_3_out, or_4_out, or_5_out, or_6_out, or_7_out;
  wire [6:0] plarom_1_p2;

  not not_1 (not_1_out, in_5);
  not not_2 (not_2_out, in_6);
  not not_3 (not_3_out, in_7);
  not not_4 (not_4_out, in_8);
  // PlaRom #(.Contents("1*7 2 1 1 2 1*3 2 2 1 2 1*3 2 1 2 1 2 2 1 1 2*4 1*3 2 1 1 2 2 1 2 1 2 1 2*4 1 1 2 2 1 2*4 1 2*4 0 1*6 0*4 1 1 0 1 0 1 1 0 1*3 0 0 1*6 0 0 1 1 0 1 1 0 1 1 0 1*6 0 1 0*4 1*12 0 1*7 0 1*8 0*3 1*3 0 0 1 1 0 1*4 0 1*4 0 0 1*4 0*3 1"), .\and (16), .outputs(7)) plarom_1: pin names not known; wires that end beside it: {in_4, in_3, in_2, in_1}, plarom_1_p2
  and and_1 (and_1_out, not_4_out, not_3_out, not_2_out, not_1_out);
  and and_2 (and_2_out, in_8, not_3_out, not_2_out, not_1_out);
  and and_3 (and_3_out, not_4_out, in_7, not_2_out, not_1_out);
  and and_4 (and_4_out, in_8, in_7, not_2_out, not_1_out);
  and and_5 (and_5_out, not_4_out, not_3_out, in_6, not_1_out);
  and and_6 (and_6_out, in_8, not_3_out, in_6, not_1_out);
  and and_7 (and_7_out, not_4_out, in_7, in_6, not_1_out);
  and and_8 (and_8_out, in_8, in_7, in_6, not_1_out);
  and and_9 (and_9_out, not_4_out, not_3_out, not_2_out, in_5);
  and and_10 (and_10_out, in_8, not_3_out, not_2_out, in_5);
  and and_11 (and_11_out, not_4_out, in_7, not_2_out, in_5);
  and and_12 (and_12_out, in_8, in_7, not_2_out, in_5);
  and and_13 (and_13_out, not_4_out, not_3_out, in_6, in_5);
  and and_14 (and_14_out, in_8, not_3_out, in_6, in_5);
  and and_15 (and_15_out, not_4_out, in_7, in_6, in_5);
  and and_16 (and_16_out, in_8, in_7, in_6, in_5);
  _7_Segment_Display #(.decimalPoint("false")) u_7_segment_display_1 (
    .g(plarom_1_p2[6]), .f(plarom_1_p2[5]), .a(plarom_1_p2[0]), .b(plarom_1_p2[1]), .e(plarom_1_p2[4]),
    .d(plarom_1_p2[3]), .c(plarom_1_p2[2]));
  or or_1 (or_1_out, and_16_out, and_15_out, and_14_out, and_12_out, and_11_out, and_10_out, and_9_out, and_7_out, and_6_out, and_5_out, and_4_out, and_3_out);
  or or_2 (or_2_out, and_16_out, and_15_out, and_13_out, and_12_out, and_11_out, and_10_out, and_9_out, and_7_out, and_6_out, and_5_out, and_1_out);
  or or_3 (or_3_out, and_16_out, and_15_out, and_14_out, and_13_out, and_12_out, and_11_out, and_9_out, and_7_out, and_3_out, and_1_out);
  or or_4 (or_4_out, and_15_out, and_14_out, and_13_out, and_12_out, and_10_out, and_9_out, and_7_out, and_6_out, and_4_out, and_3_out, and_1_out);
  _7_Segment_Display #(.decimalPoint("false")) u_7_segment_display_2 (
    .g(or_1_out), .f(or_2_out), .a(or_7_out), .b(or_6_out), .e(or_3_out), .d(or_4_out), .c(or_5_out));
  or or_5 (or_5_out, and_14_out, and_12_out, and_11_out, and_10_out, and_9_out, and_8_out, and_7_out, and_6_out, and_5_out, and_4_out, and_2_out, and_1_out);
  or or_6 (or_6_out, and_14_out, and_11_out, and_10_out, and_9_out, and_8_out, and_5_out, and_4_out, and_3_out, and_2_out, and_1_out);
  or or_7 (or_7_out, and_16_out, and_15_out, and_13_out, and_11_out, and_10_out, and_9_out, and_8_out, and_7_out, and_6_out, and_4_out, and_3_out, and_1_out);
endmodule
