// Logisim project 24125102_02.circ as structural Verilog: 1 circuit, main circuit main
module main (
  input  in_1,
  input  in_2,
  input  in_3,
  input  in_4,
  input  in_5,
  input  in_6,
  input  in_7,
  input  in_8
);

  wire and_1_out, and_2_out, and_3_out, and_4_out, and_5_out, and_6_out, and_7_out, and_8_out, and_9_out,
       and_10_out, and_11_out, and_12_out, and_13_out, and_14_out, and_15_out, and_16_out, and_17_out,
       and_18_out, and_19_out, and_20_out, and_21_out, not_1_out, not_2_out, not_3_out, not_4_out, or_1_out,
       or_2_out, or_3_out, or_4_out, or_5_out, or_6_out, or_7_out;
  wire [6:0] plarom_1_p2;

  not not_1 (not_1_out, in_1);
  not not_2 (not_2_out, in_2);
  not not_3 (not_3_out, in_3);
  not not_4 (not_4_out, in_4);
  and and_1 (and_1_out, not_1_out, not_2_out, not_3_out, in_4);
  and and_2 (and_2_out, not_1_out, in_2, not_3_out, not_4_out);
  and and_3 (and_3_out, in_1, in_2, not_3_out, in_4);
  and and_4 (and_4_out, in_1, not_2_out, in_3, in_4);
  and and_5 (and_5_out, in_1, in_3, in_4);
  and and_6 (and_6_out, in_1, in_2, not_4_out);
  and and_7 (and_7_out, in_2, in_3, not_4_out);
  and and_8 (and_8_out, not_1_out, in_2, not_3_out, in_4);
  and and_9 (and_9_out, in_1, in_2, in_3);
  and and_10 (and_10_out, not_1_out, not_2_out, in_3, not_4_out);
  and and_11 (and_11_out, in_2, in_3, in_4);
  and and_12 (and_12_out, in_1, not_2_out, in_3, not_4_out);
  and and_13 (and_13_out, not_1_out, in_4);
  and and_14 (and_14_out, not_1_out, in_2, not_3_out);
  and and_15 (and_15_out, not_2_out, not_3_out, in_4);
  and and_16 (and_16_out, not_1_out, not_2_out, in_4);
  and and_17 (and_17_out, not_1_out, in_3, in_4);
  and and_18 (and_18_out, not_1_out, not_2_out, in_3);
  and and_19 (and_19_out, not_1_out, not_2_out, not_3_out);
  and and_20 (and_20_out, in_1, in_2, not_3_out, not_4_out);
  and and_21 (and_21_out, not_1_out, in_2, in_3, in_4);
  or or_1 (or_1_out, and_1_out, and_2_out, and_3_out, and_4_out);
  or or_2 (or_2_out, and_5_out, and_6_out, and_7_out, and_8_out);
  or or_3 (or_3_out, and_6_out, and_9_out, and_10_out);
  or or_4 (or_4_out, and_1_out, and_2_out, and_11_out, and_12_out);
  or or_5 (or_5_out, and_13_out, and_14_out, and_15_out);
  _7_Segment_Display #(.active("false"), .decimalPoint("false")) u_7_segment_display_1 (
    .g(or_7_out), .f(or_6_out), .a(or_1_out), .b(or_2_out), .e(or_5_out), .d(or_4_out), .c(or_3_out));
  or or_6 (or_6_out, and_3_out, and_16_out, and_17_out, and_18_out);
  or or_7 (or_7_out, and_19_out, and_20_out, and_21_out);
  // PlaRom #(.Contents("1*7 2 1 1 2 1*3 2 2 1 2 1*3 2 1 2 1 2 2 1 1 2*4 1*3 2 1 1 2 2 1 2 1 2 1 2*4 1 1 2 2 1 2*4 1 2*4 1 0*6 1*4 0 0 1 0 1 0 0 1 0*3 1 1 0*6 1 1 0 0 1 0 0 1 0 0 1 0*6 1 0 1*4 0*12 1 0*7 1 0*8 1*3 0*3 1 1 0 0 1 0*4 1 0*4 1 1 0*4 1*3 0"), .\and (16), .outputs(7)) plarom_1: pin names not known; wires that end beside it: {in_5, in_6, in_7, in_8}, plarom_1_p2
  _7_Segment_Display #(.active("false"), .decimalPoint("false")) u_7_segment_display_2 (
    .g(plarom_1_p2[6]), .f(plarom_1_p2[5]), .a(plarom_1_p2[0]), .b(plarom_1_p2[1]), .e(plarom_1_p2[4]),
    .d(plarom_1_p2[3]), .c(plarom_1_p2[2]));
endmodule
