// Logisim project 24125102_03.circ as structural Verilog: 1 circuit, main circuit main
module main (
  input  in_1,
  input  in_2,
  input  in_3,
  input  in_4,
  output out_5,
  output out_6
);

  wire and_1_out, not_2_out;

  // NOT_Gate not_1 has open pins: in=in_1, out=open
  not not_2 (not_2_out, in_2);
  // NOT_Gate not_3 has open pins: in=in_3, out=open
  // NoConnect on in_4
  and and_1 (and_1_out, not_2_out, in_3);
  or or_1 (out_5, in_1, in_2);
  or or_2 (out_6, in_1, and_1_out);
endmodule
