// Logisim project 24125102_04.circ as structural Verilog: 1 circuit, main circuit main
module main (
  input  in_1,
  input  in_2,
  input  in_3,
  input  in_4,
  output out_5,
  output out_6,
  output out_7,
  output out_8,
  output out_9,
  output out_10,
  output out_11,
  output out_12,
  output out_13,
  output out_14,
  output out_15,
  output out_16,
  output out_17,
  output out_18,
  output out_19,
  output out_20
);

  wire decoder_1_out0, decoder_1_out1, decoder_1_out2, decoder_1_out3;

  Decoder #(.select(2)) decoder_1 (
    .out0(decoder_1_out0), .out1(decoder_1_out1), .out2(decoder_1_out2), .out3(decoder_1_out3),
    .sel({in_1, in_2}));  // open: en
  Decoder #(.select(2)) decoder_2 (
    .out0(out_5), .out1(out_6), .out2(out_7), .out3(out_8), .sel({in_3, in_4}), .en(decoder_1_out0));
  Decoder #(.select(2)) decoder_3 (
    .out0(out_9), .out1(out_10), .out2(out_11), .out3(out_12), .sel({in_3, in_4}), .en(decoder_1_out1));
  Decoder #(.select(2)) decoder_4 (
    .out0(out_13), .out1(out_14), .out2(out_15), .out3(out_16), .sel({in_3, in_4}), .en(decoder_1_out2));
  Decoder #(.select(2)) decoder_5 (
    .out0(out_17), .out1(out_18), .out2(out_19), .out3(out_20), .sel({in_3, in_4}), .en(decoder_1_out3));
endmodule
