// Logisim project 24125102_05.circ as structural Verilog: 1 circuit, main circuit main
module main (
  input  in_1,
  input  in_2,
  input  in_3,
  input  in_4,
  input  in_5,
  input  in_6,
  output out_7
);

  wire multiplexer_1_out, multiplexer_2_out, not_1_out;

  Multiplexer #(.enable("true")) multiplexer_1 (
    .in0(in_1), .in1(in_2), .out(multiplexer_1_out), .sel(in_6), .en(not_1_out));
  Multiplexer #(.enable("true")) multiplexer_2 (.in0(in_3), .in1(in_4), .out(multiplexer_2_out), .sel(in_6), .en(in_5));
  not not_1 (not_1_out, in_5);
  or or_1 (out_7, multiplexer_1_out, multiplexer_2_out);
endmodule
