// Logisim project 24125102_06.circ as structural Verilog: 1 circuit, main circuit main
module main (
  input  _4_1_MUX,
  input  _8_1_MUX,
  input  in_3,
  input  in_4,
  input  in_5,
  input  in_6,
  input  in_7,
  input  in_8,
  input  in_9,
  input  in_10,
  input  in_11,
  input  in_12,
  input  in_13,
  input  in_14,
  input  in_15,
  input  in_16,
  input  in_17,
  input  _1_4_DEMUX,
  input  in_19,
  input  in_20,
  input  _1_8_DEMUX,
  input  in_22,
  input  in_23,
  input  in_24,
  output out_25,
  output out_26,
  output out_27,
  output out_28,
  output out_29,
  output out_30,
  output out_31,
  output out_32,
  output out_33,
  output out_34,
  output out_35,
  output out_36,
  output out_37,
  output out_38
);

  wire and_4_out, and_5_out, and_6_out, and_7_out, and_17_out, and_18_out, and_19_out, and_20_out,
       and_21_out, and_22_out, and_23_out, and_24_out, not_1_out, not_2_out, not_3_out, not_4_out, not_5_out,
       not_6_out, not_7_out, not_8_out, not_9_out, not_10_out;

  not not_1 (not_1_out, in_9);
  not not_2 (not_2_out, in_11);
  and and_1 (out_27, _1_4_DEMUX, not_3_out, not_4_out);
  not not_3 (not_3_out, in_19);
  not not_4 (not_4_out, in_20);
  and and_2 (out_28, _1_4_DEMUX, not_3_out, in_20);
  and and_3 (out_29, _1_4_DEMUX, in_19, not_4_out);
  and and_4 (and_4_out, _4_1_MUX, not_1_out, not_2_out);
  and and_5 (and_5_out, in_3, not_1_out, in_11);
  and and_6 (and_6_out, in_5, in_9, not_2_out);
  and and_7 (and_7_out, in_7, in_9, in_11);
  and and_8 (out_30, _1_4_DEMUX, in_19, in_20);
  or or_1 (out_25, and_4_out, and_5_out, and_6_out, and_7_out);
  not not_5 (not_5_out, in_22);
  not not_6 (not_6_out, in_23);
  not not_7 (not_7_out, in_24);
  and and_9 (out_31, _1_8_DEMUX, not_5_out, not_6_out, not_7_out);
  and and_10 (out_32, _1_8_DEMUX, not_5_out, not_6_out, in_24);
  not not_8 (not_8_out, in_15);
  not not_9 (not_9_out, in_16);
  not not_10 (not_10_out, in_17);
  and and_11 (out_33, _1_8_DEMUX, not_5_out, in_23, not_7_out);
  and and_12 (out_34, _1_8_DEMUX, not_5_out, in_23, in_24);
  and and_13 (out_35, _1_8_DEMUX, in_22, not_6_out, not_7_out);
  and and_14 (out_36, _1_8_DEMUX, in_22, not_6_out, in_24);
  and and_15 (out_37, _1_8_DEMUX, in_22, in_23, not_7_out);
  and and_16 (out_38, _1_8_DEMUX, in_22, in_23, in_24);
  and and_17 (and_17_out, _8_1_MUX, not_8_out, not_9_out, not_10_out);
  and and_18 (and_18_out, in_4, not_8_out, not_9_out, in_17);
  and and_19 (and_19_out, in_6, not_8_out, in_16, not_10_out);
  and and_20 (and_20_out, in_8, not_8_out, in_16, in_17);
  and and_21 (and_21_out, in_10, in_15, not_9_out, not_10_out);
  and and_22 (and_22_out, in_12, in_15, not_9_out, in_17);
  and and_23 (and_23_out, in_13, in_15, in_16, not_10_out);
  and and_24 (and_24_out, in_14, in_15, in_16, in_17);
  or or_2 (out_26, and_17_out, and_18_out, and_19_out, and_20_out, and_21_out, and_22_out, and_23_out, and_24_out);
endmodule
