// Logisim project 24125102_07.circ as structural Verilog: 1 circuit, main circuit main
module main (
  input  Aa,
  input  Ab,
  input  Ba,
  input  Bb,
  input  Ca,
  input  Cb,
  output out_7,
  output out_8
);

  wire n74153_1_pin10, n74153_1_pin11, n74153_1_pin12, n74153_1_pin13, n74153_2_pin10, n74153_2_pin11,
       n74153_2_pin12, n74153_2_pin13;

  _74153 u_74153_1 (
    .pin2(Ba), .pin14(Ca), .pin13(n74153_1_pin13), .pin12(n74153_1_pin12), .pin11(n74153_1_pin11),
    .pin10(n74153_1_pin10), .pin9(out_7));  // open: pin1, pin3, pin4, pin5, pin6, pin7, pin15
  not not_1 (n74153_1_pin10, Aa);
  // NoConnect on Ab
  _74153 u_74153_2 (
    .pin2(Bb), .pin14(Cb), .pin13(n74153_2_pin13), .pin12(n74153_2_pin12), .pin11(n74153_2_pin11),
    .pin10(n74153_2_pin10), .pin9(out_8));  // open: pin1, pin3, pin4, pin5, pin6, pin7, pin15
  // also tied to GND on the sheet: {n74153_1_pin11, n74153_2_pin12}
  // also tied to VCC on the sheet: {n74153_1_pin13, n74153_1_pin12, n74153_2_pin13, n74153_2_pin11, n74153_2_pin10}

  // Notes on the sheet:
  //   Y = BC + ~A~B~C + B~C
  //   Y = ~ABC + ~(B~C) + BC
endmodule
